# Fritzing sketch schema di montaggio (saved by Fritzing 0.9.3b)
breadboards: 1

parts:
  Componente1 = Arduino Yun
  U1 = G3VM-61E1 [package=g3vm-61e1]
  U2 = G3VM-61E1 [package=g3vm-61e1]
  S1 = Pushbutton [package="[SMD]"]
  S2 = Pushbutton [package="[SMD]"]
  Componente2 = Ambient Light Sensor (TEMT6000 Breakout Board)
  T1 = LM35 Temperature Sensor [package="TO92 [THT]"]
  J2 = Basic Servo
  J1 = Basic Servo

nets:
  N1: Componente1.A0, Componente2.S
  N2: Componente1.A1, T1.Vout
  VCC: Componente1.5V, Componente1.D5_PWM, Componente1.D6_PWM, U1.P$1, U2.P$1, U2.P$3, S1.Pin_1, S1.Pin_2, S1.Pin_3, S1.Pin_4, S2.Pin_1, S2.Pin_2, S2.Pin_3, S2.Pin_4, Componente2.VCC, T1.+Vs, J2.vcc, J1.vcc
  N3: Componente1.D10_PWM/SS, J1.pulse
  N4: Componente1.D11_PWM/MOSI, J2.pulse
  N5: Componente1.D12/MISO, U1.P$2
  N6: Componente1.D13/SCK, U2.P$2
  GND: Componente1.GND, U1.P$3, Componente2.GND, T1.GND, J2.gnd, J1.gnd

notes:
  Light Relays and Light Buttons
  Light and Temperature Sensor
  Curtains servo motors
